// Logisim project cpu.circ as structural Verilog: 13 circuits, main circuit main
module main (
  input  Clock,
  input  RESET,
  input  [31:0] Instruction,
  output End,
  output Error,
  output [31:0] x0,
  output [31:0] x1,
  output [31:0] x2,
  output [31:0] x3,
  output [31:0] x4,
  output [31:0] x5,
  output [31:0] x6,
  output [31:0] x7,
  output [31:0] x8,
  output [31:0] x9,
  output [31:0] x10,
  output [31:0] x11,
  output [31:0] x12,
  output [31:0] x13,
  output [31:0] x14,
  output [31:0] x15,
  output [31:0] x16,
  output [31:0] x17,
  output [31:0] x18,
  output [31:0] x19,
  output [31:0] x20,
  output [31:0] x21,
  output [31:0] x22,
  output [31:0] x23,
  output [31:0] x24,
  output [31:0] x25,
  output [31:0] x26,
  output [31:0] x27,
  output [31:0] x28,
  output [31:0] x29,
  output [31:0] x30,
  output [31:0] x31,
  output [31:0] PC
);

  wire and_1_out, and_2_out, and_3_out, and_5_out, and_8_out, and_11_out, and_14_out, comparator_1_eq,
       comparator_2_eq, comparator_3_eq, comparator_4_eq, comparator_5_eq, comparator_6_eq, comparator_7_eq,
       comparator_8_eq, comparator_9_eq, comparator_10_eq, comparator_11_eq, comparator_12_eq,
       comparator_13_eq, comparator_14_eq, comparator_15_eq, comparator_16_eq, d_ff_1_q, d_ff_2_q, d_ff_3_q,
       d_ff_4_q, d_ff_5_q, d_ff_6_q, d_ff_11_q, EX_ALU_1, EX_ALU_2, EX_BComp_U, EX_Br, EX_Eq, EX_LT,
       GC_EX_Kill, GC_JALRn_2, GC_Reg_WEn_n_1, GC_Reg_WEn_n_2, GC_Reg_WEn_n_3, GC_rs1Dn_1, GC_rs1Dn_2,
       GC_rs1FWD_t, GC_rs2Dn_1, GC_rs2Dn_2, GC_rs2FWD_t, GC_Stall, IF_ALU_1, IF_ALU_2, IF_Br,
       multiplexer_1_out, multiplexer_2_out, multiplexer_3_out, multiplexer_4_out, multiplexer_7_out,
       multiplexer_8_out, not_1_out, not_2_out, or_1_out, or_3_out, or_4_out, or_5_out, xor_1_out;
  wire [1:0] EX_BComp, GC_WB_Seln_1, GC_WB_Seln_2, GC_WB_Seln_3, register_1_q, register_20_q;
  wire [2:0] EX_Imm_Enc, IF_Imm_Enc;
  wire [3:0] EX_ALU_Op, IF_ALU_Op;
  wire [4:0] GC_RDn_1, GC_RDn_2, GC_RDn_3, register_2_q, register_19_q;
  wire [20:0] WB_MC;
  wire [22:0] EX_MC, IF_MC, MR_MC, multiplexer_14_out, multiplexer_15_out, RR_MC;
  wire [31:0] adder_3_out, EX_ALU_Out, EX_Imm, EX_Instr, EX_PC, EX_rs1D, EX_rs2D, GC_ALUn_1, GC_ALUn_2,
       GC_ALUn_3, GC_CorrJump, GC_PC_4n_1, GC_PC_4n_2, GC_PC_4n_3, GC_RAMn_2, GC_RAMn_3, GC_rs1FWD,
       GC_rs2FWD, GC_WBData_n_1, GC_WBData_n_2, GC_WBData_n_3, IF_Jump, IF_PC_4, imm_decoder_1_immediate,
       MR_ALU_Out, MR_data, MR_Instr, MR_PC, MR_PC_4, MR_RAM_Out, MR_rs2D, MR_WB_Data, multiplexer_5_out,
       multiplexer_9_out, multiplexer_10_out, multiplexer_11_out, multiplexer_12_out, multiplexer_13_out,
       multiplexer_18_out, multiplexer_19_out, multiplexer_24_out, multiplexer_27_out, register_3_q,
       register_4_q, register_21_q, RR_EX_rs1_q, RR_EX_rs2_q, RR_Instr, RR_PC, RR_rs1, RR_rs2, WB_Instr,
       WB_WBData;

  Register #(.width(2)) register_1 (.D(IF_MC[2:1]), .Q(register_1_q), .clk(Clock), .clr(RESET));  // open: en
  Register #(.width(5)) register_2 (.D(Instruction[11:7]), .Q(register_2_q), .clk(Clock), .clr(RESET));  // open: en
  D_Flip_Flop d_ff_1 (.clk(Clock), .D(IF_MC[0]), .Q(d_ff_1_q), .reset(RESET));  // open: Qn, preset, en
  Comparator #(.width(2)) comparator_1 (.a(2'b10), .b(register_1_q), .eq(comparator_1_eq));  // open: gt, lt
  Comparator #(.width(5)) comparator_2 (.a({5{1'b0}}), .b(Instruction[19:15]), .eq(comparator_2_eq));  // open: gt, lt
  and and_1 (and_1_out, IF_ALU_1, ~comparator_2_eq, comparator_3_eq);  // AND_Gate
  Comparator #(.width(5)) comparator_3 (
    .a(Instruction[19:15]), .b(register_2_q), .eq(comparator_3_eq));  // open: gt, lt
  Comparator #(.width(5)) comparator_4 (
    .a(register_2_q), .b(Instruction[24:20]), .eq(comparator_4_eq));  // open: gt, lt
  and and_2 (and_2_out, comparator_4_eq, ~comparator_5_eq, IF_ALU_2);  // AND_Gate
  Comparator #(.width(5)) comparator_5 (.a(Instruction[24:20]), .b({5{1'b0}}), .eq(comparator_5_eq));  // open: gt, lt
  Imm_Decoder imm_decoder_1 (
    .Imm_Bits(Instruction[31:7]), .Immediate(imm_decoder_1_immediate), .Imm_Encoding(IF_Imm_Enc));
  or or_1 (or_1_out, and_1_out, and_2_out);
  Multiplexer #(.enable("false")) multiplexer_1 (.in0(1'b0), .in1(1'b0), .out(multiplexer_1_out), .sel(GC_EX_Kill));
  and and_3 (and_3_out, IF_MC[14], IF_ALU_1);
  Adder #(.width(32)) adder_1 (.a(32'h4), .b(PC), .out(IF_PC_4));  // open: cin, cout
  Adder #(.width(32)) adder_2 (.a(PC), .b(imm_decoder_1_immediate), .out(IF_Jump));  // open: cin, cout
  and and_4 (GC_Stall, or_1_out, d_ff_1_q, comparator_1_eq);
  Register #(.width(32)) register_3 (.D(IF_PC_4), .Q(register_3_q), .clk(Clock), .clr(RESET));  // open: en
  Register #(.width(32)) register_4 (.D(register_3_q), .Q(register_4_q), .clk(Clock), .clr(RESET));  // open: en
  D_Flip_Flop d_ff_2 (.clk(Clock), .D(multiplexer_1_out), .Q(d_ff_2_q), .reset(RESET));  // open: Qn, preset, en
  Multiplexer #(.enable("false")) multiplexer_2 (.in0(d_ff_2_q), .in1(1'b0), .out(multiplexer_2_out), .sel(GC_EX_Kill));
  D_Flip_Flop d_ff_3 (.clk(Clock), .D(multiplexer_3_out), .Q(d_ff_3_q), .reset(RESET));  // open: Qn, preset, en
  Multiplexer #(.enable("false")) multiplexer_3 (.in0(IF_Br), .in1(1'b0), .out(multiplexer_3_out), .sel(GC_EX_Kill));
  D_Flip_Flop d_ff_4 (.clk(Clock), .D(multiplexer_4_out), .Q(d_ff_4_q), .reset(RESET));  // open: Qn, preset, en
  Multiplexer #(.enable("false")) multiplexer_4 (
    .in0(and_3_out), .in1(1'b0), .out(multiplexer_4_out), .sel(GC_EX_Kill));
  Multiplexer #(.width(32), .enable("false")) multiplexer_5 (
    .in0(register_4_q), .in1(EX_ALU_Out), .out(multiplexer_5_out), .sel(EX_Br));
  Multiplexer #(.width(32), .enable("false")) multiplexer_6 (
    .in0(multiplexer_5_out), .in1(EX_ALU_Out), .out(GC_CorrJump), .sel(GC_JALRn_2));
  D_Flip_Flop d_ff_5 (.clk(Clock), .D(multiplexer_2_out), .Q(d_ff_5_q), .reset(RESET));  // open: Qn, preset, en
  Multiplexer #(.enable("false")) multiplexer_7 (.in0(d_ff_3_q), .in1(1'b0), .out(multiplexer_7_out), .sel(GC_EX_Kill));
  Multiplexer #(.enable("false")) multiplexer_8 (.in0(d_ff_4_q), .in1(1'b0), .out(multiplexer_8_out), .sel(GC_EX_Kill));
  Multiplexer #(.width(32), .enable("false")) multiplexer_9 (
    .in0(IF_PC_4), .in1(IF_Jump), .out(multiplexer_9_out), .sel(IF_MC[14]));
  Multiplexer #(.width(32), .enable("false")) multiplexer_10 (
    .in0(IF_PC_4), .in1(IF_Jump), .out(multiplexer_10_out), .sel(1'b0));
  xor xor_1 (xor_1_out, EX_Br, d_ff_5_q);
  and and_5 (and_5_out, xor_1_out, d_ff_6_q);
  D_Flip_Flop d_ff_6 (.clk(Clock), .D(multiplexer_7_out), .Q(d_ff_6_q), .reset(RESET));  // open: Qn, preset, en
  D_Flip_Flop d_ff_7 (.clk(Clock), .D(multiplexer_8_out), .Q(GC_JALRn_2), .reset(RESET));  // open: Qn, preset, en
  Multiplexer #(.width(32), .enable("false")) multiplexer_11 (
    .in0(multiplexer_12_out), .in1(PC), .out(multiplexer_11_out), .sel(GC_Stall));
  Multiplexer #(.width(32), .enable("false")) multiplexer_12 (
    .in0(multiplexer_9_out), .in1(multiplexer_10_out), .out(multiplexer_12_out), .sel(IF_Br));
  or or_2 (GC_EX_Kill, and_5_out, GC_JALRn_2);
  Multiplexer #(.width(32), .enable("false")) multiplexer_13 (
    .in0(multiplexer_11_out), .in1(GC_CorrJump), .out(multiplexer_13_out), .sel(GC_EX_Kill));
  Register #(.width(32)) u_PC (.D(multiplexer_13_out), .Q(PC), .clk(Clock), .clr(RESET));  // open: en
  Microcode microcode_1 (
    .Instr(Instruction),
    .Microcode({IF_MC[22:21], IF_Imm_Enc, IF_MC[17:14], IF_Br, IF_ALU_1, IF_ALU_2, IF_ALU_Op, IF_MC[6:0]}));
  or or_3 (or_3_out, GC_EX_Kill, GC_Stall);
  Register #(.width(32)) IF_RR_PC (.D(PC), .Q(RR_PC), .clk(Clock), .clr(RESET));  // open: en
  Register #(.width(32)) IF_RR_Instr (.D(Instruction), .Q(RR_Instr), .clk(Clock), .clr(RESET));  // open: en
  Multiplexer #(.width(23), .enable("false")) multiplexer_14 (
    .in0({IF_MC[22:21], IF_Imm_Enc, IF_MC[17:14], IF_Br, IF_ALU_1, IF_ALU_2, IF_ALU_Op, IF_MC[6:0]}),
    .in1({23{1'b0}}), .out(multiplexer_14_out), .sel(or_3_out));
  Register #(.width(23)) IF_RR_MC (.D(multiplexer_14_out), .Q(RR_MC), .clk(Clock), .clr(RESET));  // open: en
  Regs regs_1 (
    .Write_Data(WB_WBData), .clk(Clock), .RESET(RESET), .Reg1(RR_Instr[19:15]), .Reg2(RR_Instr[24:20]),
    .Wr_Reg(WB_Instr[11:7]), .wen(WB_MC[0]), .Reg1_Data(RR_rs1), .Reg2_Data(RR_rs2), .x0(x0), .x1(x1),
    .x2(x2), .x3(x3), .x4(x4), .x5(x5), .x6(x6), .x7(x7), .x16(x16), .x17(x17), .x18(x18), .x19(x19),
    .x20(x20), .x21(x21), .x22(x22), .x23(x23), .x8(x8), .x9(x9), .x10(x10), .x11(x11), .x12(x12), .x13(x13),
    .x14(x14), .x15(x15), .x24(x24), .x25(x25), .x26(x26), .x27(x27), .x28(x28), .x29(x29), .x30(x30),
    .x31(x31));
  Multiplexer #(.width(23), .enable("false")) multiplexer_15 (
    .in0(RR_MC), .in1({23{1'b0}}), .out(multiplexer_15_out), .sel(GC_EX_Kill));
  Register #(.width(32)) RR_EX_rs1 (.D(RR_rs1), .Q(RR_EX_rs1_q), .clk(Clock), .clr(RESET));  // open: en
  Multiplexer #(.width(32), .enable("false")) multiplexer_16 (
    .in0(RR_EX_rs1_q), .in1(GC_rs1FWD), .out(EX_rs1D), .sel(GC_rs1FWD_t));
  Register #(.width(32)) RR_EX_rs2 (.D(RR_rs2), .Q(RR_EX_rs2_q), .clk(Clock), .clr(RESET));  // open: en
  Multiplexer #(.width(32), .enable("false")) multiplexer_17 (
    .in0(RR_EX_rs2_q), .in1(GC_rs2FWD), .out(EX_rs2D), .sel(GC_rs2FWD_t));
  Register #(.width(32)) RR_EX_PC (.D(RR_PC), .Q(EX_PC), .clk(Clock), .clr(RESET));  // open: en
  Register #(.width(32)) RR_EX_Instr (.D(RR_Instr), .Q(EX_Instr), .clk(Clock), .clr(RESET));  // open: en
  Register #(.width(23)) RR_EX_MC (
    .D(multiplexer_15_out),
    .Q({EX_MC[22:21], EX_Imm_Enc, EX_BComp_U, EX_BComp, EX_MC[14:13], EX_ALU_1, EX_ALU_2, EX_ALU_Op, EX_MC[6:0]}),
    .clk(Clock), .clr(RESET));  // open: en
  Register #(.width(5)) register_5 (.D(EX_Instr[11:7]), .Q(GC_RDn_1), .clk(Clock), .clr(RESET));  // open: en
  Adder #(.width(32)) adder_3 (.a(EX_PC), .b(32'h4), .out(adder_3_out));  // open: cin, cout
  Register #(.width(32)) register_6 (.D(adder_3_out), .Q(GC_PC_4n_1), .clk(Clock), .clr(RESET));  // open: en
  Register #(.width(32)) register_7 (.D(EX_ALU_Out), .Q(GC_ALUn_1), .clk(Clock), .clr(RESET));  // open: en
  Register #(.width(2)) register_8 (.D(EX_MC[2:1]), .Q(GC_WB_Seln_1), .clk(Clock), .clr(RESET));  // open: en
  D_Flip_Flop d_ff_8 (.clk(Clock), .D(EX_MC[0]), .Q(GC_Reg_WEn_n_1), .reset(RESET));  // open: Qn, preset, en
  Register #(.width(5)) register_9 (.D(GC_RDn_1), .Q(GC_RDn_2), .clk(Clock), .clr(RESET));  // open: en
  Register #(.width(32)) register_10 (.D(GC_PC_4n_1), .Q(GC_PC_4n_2), .clk(Clock), .clr(RESET));  // open: en
  Register #(.width(32)) register_11 (.D(GC_ALUn_1), .Q(GC_ALUn_2), .clk(Clock), .clr(RESET));  // open: en
  Register #(.width(32)) register_12 (.D(MR_WB_Data), .Q(GC_RAMn_2), .clk(Clock), .clr(RESET));  // open: en
  Register #(.width(2)) register_13 (.D(GC_WB_Seln_1), .Q(GC_WB_Seln_2), .clk(Clock), .clr(RESET));  // open: en
  D_Flip_Flop d_ff_9 (.clk(Clock), .D(GC_Reg_WEn_n_1), .Q(GC_Reg_WEn_n_2), .reset(RESET));  // open: Qn, preset, en
  Register #(.width(5)) register_14 (.D(GC_RDn_2), .Q(GC_RDn_3), .clk(Clock), .clr(RESET));  // open: en
  Register #(.width(32)) register_15 (.D(GC_PC_4n_2), .Q(GC_PC_4n_3), .clk(Clock), .clr(RESET));  // open: en
  Register #(.width(32)) register_16 (.D(GC_ALUn_2), .Q(GC_ALUn_3), .clk(Clock), .clr(RESET));  // open: en
  Register #(.width(32)) register_17 (.D(GC_RAMn_2), .Q(GC_RAMn_3), .clk(Clock), .clr(RESET));  // open: en
  Register #(.width(2)) register_18 (.D(GC_WB_Seln_2), .Q(GC_WB_Seln_3), .clk(Clock), .clr(RESET));  // open: en
  D_Flip_Flop d_ff_10 (.clk(Clock), .D(GC_Reg_WEn_n_2), .Q(GC_Reg_WEn_n_3), .reset(RESET));  // open: Qn, preset, en
  Imm_Decoder imm_decoder_2 (.Imm_Bits(EX_Instr[31:7]), .Immediate(EX_Imm), .Imm_Encoding(EX_Imm_Enc));
  Branch_Comp branch_comp_1 (.rs1(EX_rs1D), .Unsign(EX_BComp_U), .rs2(EX_rs2D), .Eq(EX_Eq), .LT(EX_LT));
  Multiplexer #(.width(32), .enable("false")) multiplexer_18 (
    .in0(EX_PC), .in1(EX_rs1D), .out(multiplexer_18_out), .sel(EX_ALU_1));
  Multiplexer #(.width(32), .enable("false")) multiplexer_19 (
    .in0(EX_Imm), .in1(EX_rs2D), .out(multiplexer_19_out), .sel(EX_ALU_2));
  not not_1 (not_1_out, EX_LT);
  not not_2 (not_2_out, EX_Eq);
  ALU alu_1 (.In_1(multiplexer_18_out), .In_2(multiplexer_19_out), .Out(EX_ALU_Out), .Op(EX_ALU_Op));
  Multiplexer #(.select(2), .enable("false")) multiplexer_20 (
    .in0(EX_LT), .in1(not_1_out), .in2(EX_Eq), .in3(not_2_out), .out(EX_Br), .sel(EX_BComp));
  Comparator #(.width(5)) comparator_6 (.a(GC_RDn_1), .b(EX_Instr[19:15]), .eq(comparator_6_eq));  // open: gt, lt
  Comparator #(.width(5)) comparator_7 (.a(GC_RDn_2), .b(EX_Instr[19:15]), .eq(comparator_7_eq));  // open: gt, lt
  Comparator #(.width(5)) comparator_8 (.a(EX_Instr[19:15]), .b(GC_RDn_3), .eq(comparator_8_eq));  // open: gt, lt
  Comparator #(.width(5)) comparator_9 (.a(GC_RDn_1), .b(EX_Instr[24:20]), .eq(comparator_9_eq));  // open: gt, lt
  Comparator #(.width(5)) comparator_10 (.a(GC_RDn_2), .b(EX_Instr[24:20]), .eq(comparator_10_eq));  // open: gt, lt
  Comparator #(.width(5)) comparator_11 (.a(EX_Instr[24:20]), .b(GC_RDn_3), .eq(comparator_11_eq));  // open: gt, lt
  Multiplexer #(.select(2), .width(32), .enable("false")) multiplexer_21 (
    .in0(GC_PC_4n_1), .in1(GC_ALUn_1), .in2(32'hbad), .in3(32'hbad), .out(GC_WBData_n_1), .sel(GC_WB_Seln_1));
  Multiplexer #(.select(2), .width(32), .enable("false")) multiplexer_22 (
    .in0(GC_PC_4n_2), .in1(GC_ALUn_2), .in2(GC_RAMn_2), .in3(32'hbad), .out(GC_WBData_n_2), .sel(GC_WB_Seln_2));
  Multiplexer #(.select(2), .width(32), .enable("false")) multiplexer_23 (
    .in0(GC_PC_4n_3), .in1(GC_ALUn_3), .in2(GC_RAMn_3), .in3(32'hbad), .out(GC_WBData_n_3), .sel(GC_WB_Seln_3));
  and and_6 (GC_rs1Dn_1, GC_Reg_WEn_n_1, comparator_6_eq);
  and and_7 (GC_rs1Dn_2, GC_Reg_WEn_n_2, comparator_7_eq);
  and and_8 (and_8_out, GC_Reg_WEn_n_3, comparator_8_eq);
  and and_9 (GC_rs2Dn_1, comparator_9_eq, GC_Reg_WEn_n_1);
  and and_10 (GC_rs2Dn_2, comparator_10_eq, GC_Reg_WEn_n_2);
  and and_11 (and_11_out, comparator_11_eq, GC_Reg_WEn_n_3);
  Comparator #(.width(5)) comparator_12 (.a(EX_Instr[19:15]), .b({5{1'b0}}), .eq(comparator_12_eq));  // open: gt, lt
  Comparator #(.width(5)) comparator_13 (.a(EX_Instr[24:20]), .b({5{1'b0}}), .eq(comparator_13_eq));  // open: gt, lt
  Register #(.width(32)) EX_MR_ALU_Out (.D(EX_ALU_Out), .Q(MR_ALU_Out), .clk(Clock), .clr(RESET));  // open: en
  Register #(.width(32)) EX_MR_rs2 (.D(EX_rs2D), .Q(MR_rs2D), .clk(Clock), .clr(RESET));  // open: en
  Register #(.width(32)) EX_MR_PC (.D(EX_PC), .Q(MR_PC), .clk(Clock), .clr(RESET));  // open: en
  Register #(.width(32)) EX_MR_Instr (.D(EX_Instr), .Q(MR_Instr), .clk(Clock), .clr(RESET));  // open: en
  Register #(.width(23)) EX_MR_MC (
    .D({EX_MC[22:21], EX_Imm_Enc, EX_BComp_U, EX_BComp, EX_MC[14:13], EX_ALU_1, EX_ALU_2, EX_ALU_Op, EX_MC[6:0]}),
    .Q(MR_MC), .clk(Clock), .clr(RESET));  // open: en
  and and_12 (GC_rs1FWD_t, ~comparator_12_eq, or_4_out);  // AND_Gate
  or or_4 (or_4_out, GC_rs1Dn_1, GC_rs1Dn_2, and_8_out);
  and and_13 (GC_rs2FWD_t, ~comparator_13_eq, or_5_out);  // AND_Gate
  or or_5 (or_5_out, GC_rs2Dn_1, GC_rs2Dn_2, and_11_out);
  Multiplexer #(.width(32), .enable("false")) multiplexer_24 (
    .in0(GC_WBData_n_3), .in1(GC_WBData_n_2), .out(multiplexer_24_out), .sel(GC_rs1Dn_2));
  Multiplexer #(.width(32), .enable("false")) multiplexer_25 (
    .in0(multiplexer_24_out), .in1(GC_WBData_n_1), .out(GC_rs1FWD), .sel(GC_rs1Dn_1));
  Multiplexer #(.width(32), .enable("false")) multiplexer_26 (
    .in0(multiplexer_27_out), .in1(GC_WBData_n_1), .out(GC_rs2FWD), .sel(GC_rs2Dn_1));
  Multiplexer #(.width(32), .enable("false")) multiplexer_27 (
    .in0(GC_WBData_n_3), .in1(GC_WBData_n_2), .out(multiplexer_27_out), .sel(GC_rs2Dn_2));
  Adder #(.width(32)) adder_4 (.a(32'h4), .b(MR_PC), .out(MR_PC_4));  // open: cin, cout
  RAM ram_1 (
    .ALU(MR_ALU_Out), .Write_Data(MR_data), .clk(Clock), .clr(RESET), .Wr_En(MR_MC[4]),
    .Read_Unsigned(MR_MC[3]), .RAM_Out(MR_RAM_Out), .RAM_num(MR_MC[6:5]));
  Register #(.width(5)) register_19 (.D(MR_Instr[11:7]), .Q(register_19_q), .clk(Clock), .clr(RESET));  // open: en
  Register #(.width(2)) register_20 (.D(MR_MC[2:1]), .Q(register_20_q), .clk(Clock), .clr(RESET));  // open: en
  Comparator #(.width(5)) comparator_14 (.a(MR_Instr[24:20]), .b({5{1'b0}}), .eq(comparator_14_eq));  // open: gt, lt
  Comparator #(.width(5)) comparator_15 (
    .a(MR_Instr[24:20]), .b(register_19_q), .eq(comparator_15_eq));  // open: gt, lt
  Comparator #(.width(2)) comparator_16 (.a(2'b10), .b(register_20_q), .eq(comparator_16_eq));  // open: gt, lt
  D_Flip_Flop d_ff_11 (.clk(Clock), .D(MR_MC[0]), .Q(d_ff_11_q), .reset(RESET));  // open: Qn, preset, en
  and and_14 (and_14_out, ~comparator_14_eq, comparator_15_eq, comparator_16_eq, d_ff_11_q);  // AND_Gate
  Register #(.width(32)) register_21 (.D(MR_RAM_Out), .Q(register_21_q), .clk(Clock), .clr(RESET));  // open: en
  Multiplexer #(.select(2), .width(32), .enable("false")) multiplexer_28 (
    .in0(MR_PC_4), .in1(MR_ALU_Out), .in2(MR_RAM_Out), .in3(32'hbad), .out(MR_WB_Data), .sel(MR_MC[2:1]));
  Multiplexer #(.width(32), .enable("false")) multiplexer_29 (
    .in0(MR_rs2D), .in1(register_21_q), .out(MR_data), .sel(and_14_out));
  Register #(.width(32)) MR_WB_WBData (.D(MR_WB_Data), .Q(WB_WBData), .clk(Clock), .clr(RESET));  // open: en
  Register #(.width(32)) MR_WB_Instr (.D(MR_Instr), .Q(WB_Instr), .clk(Clock), .clr(RESET));  // open: en
  Register #(.width(23)) MR_WB_MC (.D(MR_MC), .Q({Error, End, WB_MC}), .clk(Clock), .clr(RESET));  // open: en

  // Other names for the same wires on the sheet: clk = Clock; EX_rs1[4:0] = EX_Instr[19:15];
  //   EX_rs2[4:0] = EX_Instr[24:20]; EX_Reg_WEn = EX_MC[0]; EX_WB_Sel[1:0] = EX_MC[2:1];
  //   EX_MC (some bits) = {EX_Imm_Enc, EX_BComp_U, EX_BComp, EX_ALU_1, EX_ALU_2, EX_ALU_Op}; GC_Flush = GC_EX_Kill;
  //   GC_RR_BKill = GC_EX_Kill; IF_Instr[31:0] = Instruction; IF_Reg_WEn = IF_MC[0]; IF_WB_Sel[1:0] = IF_MC[2:1];
  //   IF_MC (some bits) = {IF_Imm_Enc, IF_Br, IF_ALU_1, IF_ALU_2, IF_ALU_Op}; IF_UC = IF_MC[14]; IF_PC[31:0] = PC;
  //   MR_Reg_WEn = MR_MC[0]; MR_WB_Sel[1:0] = MR_MC[2:1]; MR_RAM_Read_U = MR_MC[3]; MR_RAM_WEn = MR_MC[4];
  //   MR_RAM_num[1:0] = MR_MC[6:5]; WB_Reg_WEn = WB_MC[0]; Halt = End; WB_MC[22:21] = {Error, End};
  //   x0_Data[31:0] = x0; x1_Data[31:0] = x1; x2_Data[31:0] = x2; x3_Data[31:0] = x3; x4_Data[31:0] = x4;
  //   x5_Data[31:0] = x5; x6_Data[31:0] = x6; x7_Data[31:0] = x7; x8_Data[31:0] = x8; x9_Data[31:0] = x9;
  //   x10_Data[31:0] = x10; x11_Data[31:0] = x11; x12_Data[31:0] = x12; x13_Data[31:0] = x13; x14_Data[31:0] = x14;
  //   x15_Data[31:0] = x15; x16_Data[31:0] = x16; x17_Data[31:0] = x17; x18_Data[31:0] = x18; x19_Data[31:0] = x19;
  //   x20_Data[31:0] = x20; x21_Data[31:0] = x21; x22_Data[31:0] = x22; x23_Data[31:0] = x23; x24_Data[31:0] = x24;
  //   x25_Data[31:0] = x25; x26_Data[31:0] = x26; x27_Data[31:0] = x27; x28_Data[31:0] = x28; x29_Data[31:0] = x29;
  //   x30_Data[31:0] = x30; x31_Data[31:0] = x31
endmodule

module Regs (
  input  [31:0] Write_Data,
  input  clk,
  input  RESET,
  input  [4:0] Reg1,
  input  [4:0] Reg2,
  input  wen,
  input  [4:0] Wr_Reg,
  output [31:0] x0,
  output [31:0] x1,
  output [31:0] x2,
  output [31:0] x3,
  output [31:0] x4,
  output [31:0] x5,
  output [31:0] x6,
  output [31:0] x7,
  output [31:0] x8,
  output [31:0] x9,
  output [31:0] x10,
  output [31:0] x11,
  output [31:0] x12,
  output [31:0] x13,
  output [31:0] x14,
  output [31:0] x15,
  output [31:0] x16,
  output [31:0] x17,
  output [31:0] x18,
  output [31:0] x19,
  output [31:0] x20,
  output [31:0] x21,
  output [31:0] x22,
  output [31:0] x23,
  output [31:0] x24,
  output [31:0] x25,
  output [31:0] x26,
  output [31:0] x27,
  output [31:0] x28,
  output [31:0] x29,
  output [31:0] x30,
  output [31:0] x31,
  output [31:0] Reg1_Data,
  output [31:0] Reg2_Data
);

  wire demultiplexer_1_out0, x1_WEn, x2_WEn, x3_WEn, x4_WEn, x5_WEn, x6_WEn, x7_WEn, x8_WEn, x9_WEn, x10_WEn,
       x11_WEn, x12_WEn, x13_WEn, x14_WEn, x15_WEn, x16_WEn, x17_WEn, x18_WEn, x19_WEn, x20_WEn, x21_WEn,
       x22_WEn, x23_WEn, x24_WEn, x25_WEn, x26_WEn, x27_WEn, x28_WEn, x29_WEn, x30_WEn, x31_WEn;

  LED Write_to_x0 (.in(demultiplexer_1_out0));
  Demultiplexer #(.select(5), .disabled(0), .enable("false")) demultiplexer_1 (
    .out0(demultiplexer_1_out0), .out1(x1_WEn), .out2(x2_WEn), .out3(x3_WEn), .out4(x4_WEn), .out5(x5_WEn),
    .out6(x6_WEn), .out7(x7_WEn), .out8(x8_WEn), .out9(x9_WEn), .out10(x10_WEn), .out11(x11_WEn),
    .out12(x12_WEn), .out13(x13_WEn), .out14(x14_WEn), .out15(x15_WEn), .out16(x16_WEn), .out17(x17_WEn),
    .out18(x18_WEn), .out19(x19_WEn), .out20(x20_WEn), .out21(x21_WEn), .out22(x22_WEn), .out23(x23_WEn),
    .out24(x24_WEn), .out25(x25_WEn), .out26(x26_WEn), .out27(x27_WEn), .out28(x28_WEn), .out29(x29_WEn),
    .out30(x30_WEn), .out31(x31_WEn), .in(wen), .sel(Wr_Reg));
  Register #(.width(32)) u_x4 (.D(Write_Data), .en(x4_WEn), .Q(x4), .clk(clk), .clr(RESET));
  Register #(.width(32)) u_x8 (.D(Write_Data), .en(x8_WEn), .Q(x8), .clk(clk), .clr(RESET));
  Register #(.width(32)) u_x12 (.D(Write_Data), .en(x12_WEn), .Q(x12), .clk(clk), .clr(RESET));
  Register #(.width(32)) u_x16 (.D(Write_Data), .en(x16_WEn), .Q(x16), .clk(clk), .clr(RESET));
  Register #(.width(32)) u_x20 (.D(Write_Data), .en(x20_WEn), .Q(x20), .clk(clk), .clr(RESET));
  Register #(.width(32)) u_x24 (.D(Write_Data), .en(x24_WEn), .Q(x24), .clk(clk), .clr(RESET));
  Register #(.width(32)) u_x28 (.D(Write_Data), .en(x28_WEn), .Q(x28), .clk(clk), .clr(RESET));
  Register #(.width(32)) u_x1 (.D(Write_Data), .en(x1_WEn), .Q(x1), .clk(clk), .clr(RESET));
  Register #(.width(32)) u_x5 (.D(Write_Data), .en(x5_WEn), .Q(x5), .clk(clk), .clr(RESET));
  Register #(.width(32)) u_x9 (.D(Write_Data), .en(x9_WEn), .Q(x9), .clk(clk), .clr(RESET));
  Register #(.width(32)) u_x13 (.D(Write_Data), .en(x13_WEn), .Q(x13), .clk(clk), .clr(RESET));
  Register #(.width(32)) u_x17 (.D(Write_Data), .en(x17_WEn), .Q(x17), .clk(clk), .clr(RESET));
  Register #(.width(32)) u_x21 (.D(Write_Data), .en(x21_WEn), .Q(x21), .clk(clk), .clr(RESET));
  Register #(.width(32)) u_x25 (.D(Write_Data), .en(x25_WEn), .Q(x25), .clk(clk), .clr(RESET));
  Register #(.width(32)) u_x29 (.D(Write_Data), .en(x29_WEn), .Q(x29), .clk(clk), .clr(RESET));
  Register #(.width(32)) u_x2 (.D(Write_Data), .en(x2_WEn), .Q(x2), .clk(clk), .clr(RESET));
  Register #(.width(32)) u_x6 (.D(Write_Data), .en(x6_WEn), .Q(x6), .clk(clk), .clr(RESET));
  Register #(.width(32)) u_x10 (.D(Write_Data), .en(x10_WEn), .Q(x10), .clk(clk), .clr(RESET));
  Register #(.width(32)) u_x14 (.D(Write_Data), .en(x14_WEn), .Q(x14), .clk(clk), .clr(RESET));
  Register #(.width(32)) u_x18 (.D(Write_Data), .en(x18_WEn), .Q(x18), .clk(clk), .clr(RESET));
  Register #(.width(32)) u_x22 (.D(Write_Data), .en(x22_WEn), .Q(x22), .clk(clk), .clr(RESET));
  Register #(.width(32)) u_x26 (.D(Write_Data), .en(x26_WEn), .Q(x26), .clk(clk), .clr(RESET));
  Register #(.width(32)) u_x30 (.D(Write_Data), .en(x30_WEn), .Q(x30), .clk(clk), .clr(RESET));
  Register #(.width(32)) u_x3 (.D(Write_Data), .en(x3_WEn), .Q(x3), .clk(clk), .clr(RESET));
  Register #(.width(32)) u_x7 (.D(Write_Data), .en(x7_WEn), .Q(x7), .clk(clk), .clr(RESET));
  Register #(.width(32)) u_x11 (.D(Write_Data), .en(x11_WEn), .Q(x11), .clk(clk), .clr(RESET));
  Register #(.width(32)) u_x15 (.D(Write_Data), .en(x15_WEn), .Q(x15), .clk(clk), .clr(RESET));
  Register #(.width(32)) u_x19 (.D(Write_Data), .en(x19_WEn), .Q(x19), .clk(clk), .clr(RESET));
  Register #(.width(32)) u_x23 (.D(Write_Data), .en(x23_WEn), .Q(x23), .clk(clk), .clr(RESET));
  Register #(.width(32)) u_x27 (.D(Write_Data), .en(x27_WEn), .Q(x27), .clk(clk), .clr(RESET));
  Register #(.width(32)) u_x31 (.D(Write_Data), .en(x31_WEn), .Q(x31), .clk(clk), .clr(RESET));
  Multiplexer #(.select(5), .width(32), .enable("false")) multiplexer_1 (
    .in0({32{1'b0}}), .in1(x1), .in2(x2), .in3(x3), .in4(x4), .in5(x5), .in6(x6), .in7(x7), .in8(x8),
    .in9(x9), .in10(x10), .in11(x11), .in12(x12), .in13(x13), .in14(x14), .in15(x15), .in16(x16), .in17(x17),
    .in18(x18), .in19(x19), .in20(x20), .in21(x21), .in22(x22), .in23(x23), .in24(x24), .in25(x25),
    .in26(x26), .in27(x27), .in28(x28), .in29(x29), .in30(x30), .in31(x31), .out(Reg1_Data), .sel(Reg1));
  Multiplexer #(.select(5), .width(32), .enable("false")) multiplexer_2 (
    .in0({32{1'b0}}), .in1(x1), .in2(x2), .in3(x3), .in4(x4), .in5(x5), .in6(x6), .in7(x7), .in8(x8),
    .in9(x9), .in10(x10), .in11(x11), .in12(x12), .in13(x13), .in14(x14), .in15(x15), .in16(x16), .in17(x17),
    .in18(x18), .in19(x19), .in20(x20), .in21(x21), .in22(x22), .in23(x23), .in24(x24), .in25(x25),
    .in26(x26), .in27(x27), .in28(x28), .in29(x29), .in30(x30), .in31(x31), .out(Reg2_Data), .sel(Reg2));

  assign x0 = {32{1'b0}};

  // Other names for the same wires on the sheet: RES = RESET; WD[31:0] = Write_Data; x1_Data[31:0] = x1;
  //   x2_Data[31:0] = x2; x3_Data[31:0] = x3; x4_Data[31:0] = x4; x5_Data[31:0] = x5; x6_Data[31:0] = x6;
  //   x7_Data[31:0] = x7; x8_Data[31:0] = x8; x9_Data[31:0] = x9; x10_Data[31:0] = x10; x11_Data[31:0] = x11;
  //   x12_Data[31:0] = x12; x13_Data[31:0] = x13; x14_Data[31:0] = x14; x15_Data[31:0] = x15; x16_Data[31:0] = x16;
  //   x17_Data[31:0] = x17; x18_Data[31:0] = x18; x19_Data[31:0] = x19; x20_Data[31:0] = x20; x21_Data[31:0] = x21;
  //   x22_Data[31:0] = x22; x23_Data[31:0] = x23; x24_Data[31:0] = x24; x25_Data[31:0] = x25; x26_Data[31:0] = x26;
  //   x27_Data[31:0] = x27; x28_Data[31:0] = x28; x29_Data[31:0] = x29; x30_Data[31:0] = x30; x31_Data[31:0] = x31

  // Notes on the sheet:
  //   x0
endmodule

module Imm_Decoder (
  input  [24:0] Imm_Bits,
  input  [2:0] Imm_Encoding,
  output [31:0] Immediate
);

  wire [31:0] bit_extender_1_out, I, S, SB, U, UJ;

  assign bit_extender_1_out = {{12{Imm_Bits[24]}}, Imm_Bits[24:5]};  // Bit_Extender bit_extender_1
  assign I = {{20{Imm_Bits[24]}}, Imm_Bits[24:13]};  // Bit_Extender bit_extender_2
  assign S = {{20{Imm_Bits[24]}}, {Imm_Bits[24:18], Imm_Bits[4:0]}};  // Bit_Extender bit_extender_3
  assign SB = {{19{Imm_Bits[24]}}, {Imm_Bits[24], Imm_Bits[0], Imm_Bits[23:18], Imm_Bits[4:1], 1'b0}};  // Bit_Extender bit_extender_4
  Shifter #(.width(32)) shifter_1 (.in(bit_extender_1_out), .\dist (5'b01100), .out(U));
  assign UJ = {{11{Imm_Bits[24]}}, {Imm_Bits[24], Imm_Bits[12:5], Imm_Bits[13], Imm_Bits[23:14], 1'b0}};  // Bit_Extender bit_extender_5
  Multiplexer #(.select(3), .width(32), .disabled(0), .enable("false")) multiplexer_1 (
    .in0(I), .in1(S), .in2(SB), .in3(UJ), .in4(U), .in5(32'hbad), .in6(32'hbad), .in7(32'hbad),
    .out(Immediate), .sel(Imm_Encoding));

  // Other names for the same wires on the sheet: Enc[2:0] = Imm_Encoding
endmodule

module ALU (
  input  [31:0] In_1,
  input  [31:0] In_2,
  input  [3:0] Op,
  output [31:0] Out
);

  wire comparator_1_lt, comparator_2_lt;
  wire [31:0] add, \and , div, mul, mulh, \or , rem, sll, slt, sltu, sra, srl, sub, \xor ;

  Adder #(.width(32)) adder_1 (.a(In_1), .b(In_2), .out(add));  // open: cin, cout
  Subtractor #(.width(32)) subtractor_1 (.a(In_1), .b(In_2), .out(sub));  // open: bin, bout
  Multiplier #(.width(32)) multiplier_1 (.a(In_1), .b(In_2), .out(mul), .cout(mulh));  // open: cin
  Divider #(.width(32)) divider_1 (.a(In_1), .b(In_2), .out(div), .rem(rem));  // open: upper
  Shifter #(.width(32)) shifter_1 (.in(In_1), .\dist (In_2[4:0]), .out(sll));
  Shifter #(.width(32), .shift("lr")) shifter_2 (.in(In_1), .\dist (In_2[4:0]), .out(srl));
  Shifter #(.width(32), .shift("ar")) shifter_3 (.in(In_1), .\dist (In_2[4:0]), .out(sra));
  Comparator #(.width(32)) comparator_1 (.a(In_1), .b(In_2), .lt(comparator_1_lt));  // open: gt, eq
  Comparator #(.width(32), .mode("unsigned")) comparator_2 (.a(In_1), .b(In_2), .lt(comparator_2_lt));  // open: gt, eq
  assign \or  = In_1 | In_2;  // OR_Gate or_1, 32 bits wide
  assign \and  = In_1 & In_2;  // AND_Gate and_1, 32 bits wide
  assign \xor  = In_1 ^ In_2;  // XOR_Gate xor_1, 32 bits wide
  assign slt = {{31{1'b0}}, comparator_1_lt};  // Bit_Extender bit_extender_1
  assign sltu = {{31{1'b0}}, comparator_2_lt};  // Bit_Extender bit_extender_2
  Multiplexer #(.select(4), .width(32), .enable("false")) multiplexer_1 (
    .in0(add), .in1(sub), .in2(mul), .in3(mulh), .in4(div), .in5(rem), .in6(sll), .in7(srl), .in8(sra),
    .in9(slt), .in10(sltu), .in11(\or ), .in12(\and ), .in13(\xor ), .in14(In_2), .in15(32'hbad), .out(Out),
    .sel(Op));
endmodule

module Branch_Comp (
  input  [31:0] rs1,
  input  Unsign,
  input  [31:0] rs2,
  output Eq,
  output LT
);

  wire SEq, SLT, UEq, ULT;

  Comparator #(.width(32)) comparator_1 (.a(rs1), .b(rs2), .eq(SEq), .lt(SLT));  // open: gt
  Comparator #(.width(32), .mode("unsigned")) comparator_2 (.a(rs1), .b(rs2), .eq(UEq), .lt(ULT));  // open: gt
  Multiplexer #(.enable("false")) multiplexer_1 (.in0(SEq), .in1(UEq), .out(Eq), .sel(Unsign));
  Multiplexer #(.enable("false")) multiplexer_2 (.in0(SLT), .in1(ULT), .out(LT), .sel(Unsign));
endmodule

module RAM (
  input  [31:0] ALU,
  input  [31:0] Write_Data,
  input  clk,
  input  clr,
  input  Wr_En,
  input  [1:0] RAM_num,
  input  Read_Unsigned,
  output [31:0] RAM_Out
);

  wire [7:0] b0_out, b1_out, b2_out, b3_out;
  wire [22:0] H110;
  wire [31:0] extend_byte_s_1_out, extend_byte_s_2_out, extend_byte_s_3_out, extend_byte_s_4_out,
       extend_byte_u_1_out, extend_byte_u_2_out, extend_byte_u_3_out, extend_byte_u_4_out,
       extend_half_s_1_out, extend_half_s_2_out, extend_half_s_3_out, extend_half_s_4_out,
       extend_half_u_1_out, extend_half_u_2_out, extend_half_u_3_out, extend_half_u_4_out,
       extend_tronple_s_1_out, extend_tronple_s_2_out, extend_tronple_s_3_out, extend_tronple_s_4_out,
       extend_tronple_u_1_out, extend_tronple_u_2_out, extend_tronple_u_3_out, extend_tronple_u_4_out,
       multiplexer_1_out, multiplexer_2_out, multiplexer_3_out, multiplexer_4_out;

  Adder #(.width(23)) adder_1 (.a(ALU[24:2]), .b(23'h1), .out(H110));  // open: cin, cout
  Multiplexer #(.select(4), .width(32), .enable("false")) multiplexer_1 (
    .in0({Wr_En, Write_Data[7:0], ALU[24:2]}), .in1({32{1'b0}}), .in2({32{1'b0}}), .in3({32{1'b0}}),
    .in4({Wr_En, Write_Data[7:0], ALU[24:2]}), .in5({32{1'b0}}), .in6({32{1'b0}}),
    .in7({Wr_En, Write_Data[15:8], H110}), .in8({Wr_En, Write_Data[7:0], ALU[24:2]}), .in9({32{1'b0}}),
    .in10({Wr_En, Write_Data[23:16], H110}), .in11({Wr_En, Write_Data[15:8], H110}),
    .in12({Wr_En, Write_Data[7:0], ALU[24:2]}), .in13({Wr_En, Write_Data[31:24], H110}),
    .in14({Wr_En, Write_Data[23:16], H110}), .in15({Wr_En, Write_Data[15:8], H110}), .out(multiplexer_1_out),
    .sel({RAM_num, ALU[1:0]}));
  Multiplexer #(.select(4), .width(32), .enable("false")) multiplexer_2 (
    .in0({32{1'b0}}), .in1({Wr_En, Write_Data[7:0], ALU[24:2]}), .in2({32{1'b0}}), .in3({32{1'b0}}),
    .in4({Wr_En, Write_Data[15:8], ALU[24:2]}), .in5({Wr_En, Write_Data[7:0], ALU[24:2]}), .in6({32{1'b0}}),
    .in7({32{1'b0}}), .in8({Wr_En, Write_Data[15:8], ALU[24:2]}), .in9({Wr_En, Write_Data[7:0], ALU[24:2]}),
    .in10({32{1'b0}}), .in11({Wr_En, Write_Data[23:16], H110}), .in12({Wr_En, Write_Data[15:8], ALU[24:2]}),
    .in13({Wr_En, Write_Data[7:0], ALU[24:2]}), .in14({Wr_En, Write_Data[31:24], H110}),
    .in15({Wr_En, Write_Data[23:16], H110}), .out(multiplexer_2_out), .sel({RAM_num, ALU[1:0]}));
  Multiplexer #(.select(4), .width(32), .enable("false")) multiplexer_3 (
    .in0({32{1'b0}}), .in1({32{1'b0}}), .in2({Wr_En, Write_Data[7:0], ALU[24:2]}), .in3({32{1'b0}}),
    .in4({32{1'b0}}), .in5({Wr_En, Write_Data[15:8], ALU[24:2]}), .in6({Wr_En, Write_Data[7:0], ALU[24:2]}),
    .in7({32{1'b0}}), .in8({Wr_En, Write_Data[23:16], ALU[24:2]}),
    .in9({Wr_En, Write_Data[15:8], ALU[24:2]}), .in10({Wr_En, Write_Data[7:0], ALU[24:2]}),
    .in11({32{1'b0}}), .in12({Wr_En, Write_Data[23:16], ALU[24:2]}),
    .in13({Wr_En, Write_Data[15:8], ALU[24:2]}), .in14({Wr_En, Write_Data[7:0], ALU[24:2]}),
    .in15({Wr_En, Write_Data[31:24], H110}), .out(multiplexer_3_out), .sel({RAM_num, ALU[1:0]}));
  Multiplexer #(.select(4), .width(32), .enable("false")) multiplexer_4 (
    .in0({32{1'b0}}), .in1({32{1'b0}}), .in2({32{1'b0}}), .in3({Wr_En, Write_Data[7:0], ALU[24:2]}),
    .in4({32{1'b0}}), .in5({32{1'b0}}), .in6({Wr_En, Write_Data[15:8], ALU[24:2]}),
    .in7({Wr_En, Write_Data[7:0], ALU[24:2]}), .in8({32{1'b0}}), .in9({Wr_En, Write_Data[23:16], ALU[24:2]}),
    .in10({Wr_En, Write_Data[15:8], ALU[24:2]}), .in11({Wr_En, Write_Data[7:0], ALU[24:2]}),
    .in12({Wr_En, Write_Data[31:24], ALU[24:2]}), .in13({Wr_En, Write_Data[23:16], ALU[24:2]}),
    .in14({Wr_En, Write_Data[15:8], ALU[24:2]}), .in15({Wr_En, Write_Data[7:0], ALU[24:2]}),
    .out(multiplexer_4_out), .sel({RAM_num, ALU[1:0]}));
  RAM_part #(.addrWidth(23), .bus("separate")) ram_1 (
    .addr(multiplexer_1_out[22:0]), .din(multiplexer_1_out[30:23]), .data(b0_out),
    .str(multiplexer_1_out[31]), .clk(clk), .clr(clr));  // open: sel, ld
  RAM_part #(.addrWidth(23), .bus("separate")) ram_2 (
    .addr(multiplexer_2_out[22:0]), .din(multiplexer_2_out[30:23]), .data(b1_out),
    .str(multiplexer_2_out[31]), .clk(clk), .clr(clr));  // open: sel, ld
  RAM_part #(.addrWidth(23), .bus("separate")) ram_3 (
    .addr(multiplexer_3_out[22:0]), .din(multiplexer_3_out[30:23]), .data(b2_out),
    .str(multiplexer_3_out[31]), .clk(clk), .clr(clr));  // open: sel, ld
  RAM_part #(.addrWidth(23), .bus("separate")) ram_4 (
    .addr(multiplexer_4_out[22:0]), .din(multiplexer_4_out[30:23]), .data(b3_out),
    .str(multiplexer_4_out[31]), .clk(clk), .clr(clr));  // open: sel, ld
  Extend_Byte_S extend_byte_s_1 (.In(b0_out), .Out(extend_byte_s_1_out));
  Extend_Byte_U extend_byte_u_1 (.In(b0_out), .Out(extend_byte_u_1_out));
  Extend_Byte_S extend_byte_s_2 (.In(b1_out), .Out(extend_byte_s_2_out));
  Extend_Byte_U extend_byte_u_2 (.In(b1_out), .Out(extend_byte_u_2_out));
  Extend_Byte_S extend_byte_s_3 (.In(b2_out), .Out(extend_byte_s_3_out));
  Extend_Byte_U extend_byte_u_3 (.In(b2_out), .Out(extend_byte_u_3_out));
  Extend_Byte_S extend_byte_s_4 (.In(b3_out), .Out(extend_byte_s_4_out));
  Extend_Byte_U extend_byte_u_4 (.In(b3_out), .Out(extend_byte_u_4_out));
  Extend_Half_S extend_half_s_1 (.In({b1_out, b0_out}), .Out(extend_half_s_1_out));
  Extend_Half_U extend_half_u_1 (.In({b1_out, b0_out}), .Out(extend_half_u_1_out));
  Extend_Half_S extend_half_s_2 (.In({b2_out, b1_out}), .Out(extend_half_s_2_out));
  Extend_Half_U extend_half_u_2 (.In({b2_out, b1_out}), .Out(extend_half_u_2_out));
  Extend_Half_S extend_half_s_3 (.In({b3_out, b2_out}), .Out(extend_half_s_3_out));
  Extend_Half_U extend_half_u_3 (.In({b3_out, b2_out}), .Out(extend_half_u_3_out));
  Extend_Half_S extend_half_s_4 (.In({b0_out, b3_out}), .Out(extend_half_s_4_out));
  Extend_Half_U extend_half_u_4 (.In({b0_out, b3_out}), .Out(extend_half_u_4_out));
  Extend_Tronple_S extend_tronple_s_1 (.In({b2_out, b1_out, b0_out}), .Out(extend_tronple_s_1_out));
  Extend_Tronple_U extend_tronple_u_1 (.In({b2_out, b1_out, b0_out}), .Out(extend_tronple_u_1_out));
  Extend_Tronple_S extend_tronple_s_2 (.In({b3_out, b2_out, b1_out}), .Out(extend_tronple_s_2_out));
  Extend_Tronple_U extend_tronple_u_2 (.In({b3_out, b2_out, b1_out}), .Out(extend_tronple_u_2_out));
  Extend_Tronple_S extend_tronple_s_3 (.In({b0_out, b3_out, b2_out}), .Out(extend_tronple_s_3_out));
  Extend_Tronple_U extend_tronple_u_3 (.In({b0_out, b3_out, b2_out}), .Out(extend_tronple_u_3_out));
  Extend_Tronple_S extend_tronple_s_4 (.In({b1_out, b0_out, b3_out}), .Out(extend_tronple_s_4_out));
  Extend_Tronple_U extend_tronple_u_4 (.In({b1_out, b0_out, b3_out}), .Out(extend_tronple_u_4_out));
  Multiplexer #(.select(5), .width(32), .enable("false")) multiplexer_5 (
    .in0(extend_byte_s_1_out), .in1(extend_byte_u_1_out), .in2(extend_byte_s_2_out),
    .in3(extend_byte_u_2_out), .in4(extend_byte_s_3_out), .in5(extend_byte_u_3_out),
    .in6(extend_byte_s_4_out), .in7(extend_byte_u_4_out), .in8(extend_half_s_1_out),
    .in9(extend_half_u_1_out), .in10(extend_half_s_2_out), .in11(extend_half_u_2_out),
    .in12(extend_half_s_3_out), .in13(extend_half_u_3_out), .in14(extend_half_s_4_out),
    .in15(extend_half_u_4_out), .in16(extend_tronple_s_1_out), .in17(extend_tronple_u_1_out),
    .in18(extend_tronple_s_2_out), .in19(extend_tronple_u_2_out), .in20(extend_tronple_s_3_out),
    .in21(extend_tronple_u_3_out), .in22(extend_tronple_s_4_out), .in23(extend_tronple_u_4_out),
    .in24({b3_out, b2_out, b1_out, b0_out}), .in25({b3_out, b2_out, b1_out, b0_out}),
    .in26({b0_out, b3_out, b2_out, b1_out}), .in27({b0_out, b3_out, b2_out, b1_out}),
    .in28({b1_out, b0_out, b3_out, b2_out}), .in29({b1_out, b0_out, b3_out, b2_out}),
    .in30({b2_out, b1_out, b0_out, b3_out}), .in31({b2_out, b1_out, b0_out, b3_out}), .out(RAM_Out),
    .sel({RAM_num, ALU[1:0], Read_Unsigned}));

  // Other names for the same wires on the sheet: Byte_Index[1:0] = ALU[1:0]; Encoding[3:0] = {RAM_num, ALU[1:0]};
  //   b1[7:0] = Write_Data[15:8]; H001[31:0] = {Wr_En, Write_Data[15:8], ALU[24:2]};
  //   H012[31:0] = {Wr_En, Write_Data[15:8], ALU[24:2]}; H103[31:0] = {Wr_En, Write_Data[15:8], ALU[24:2]};
  //   H110[31:23] = {Wr_En, Write_Data[15:8]}; T001[31:0] = {Wr_En, Write_Data[15:8], ALU[24:2]};
  //   T012[31:0] = {Wr_En, Write_Data[15:8], ALU[24:2]}; T103[31:0] = {Wr_En, Write_Data[15:8], ALU[24:2]};
  //   T110[31:0] = {Wr_En, Write_Data[15:8], H110}; W001[31:0] = {Wr_En, Write_Data[15:8], ALU[24:2]};
  //   W012[31:0] = {Wr_En, Write_Data[15:8], ALU[24:2]}; W103[31:0] = {Wr_En, Write_Data[15:8], ALU[24:2]};
  //   W110[31:0] = {Wr_En, Write_Data[15:8], H110}; b2[7:0] = Write_Data[23:16];
  //   T002[31:0] = {Wr_En, Write_Data[23:16], ALU[24:2]}; T013[31:0] = {Wr_En, Write_Data[23:16], ALU[24:2]};
  //   T100[31:0] = {Wr_En, Write_Data[23:16], H110}; T111[31:0] = {Wr_En, Write_Data[23:16], H110};
  //   W002[31:0] = {Wr_En, Write_Data[23:16], ALU[24:2]}; W013[31:0] = {Wr_En, Write_Data[23:16], ALU[24:2]};
  //   W100[31:0] = {Wr_En, Write_Data[23:16], H110}; W111[31:0] = {Wr_En, Write_Data[23:16], H110};
  //   W010[31:0] = {Wr_En, Write_Data[31:24], H110}; W101[31:0] = {Wr_En, Write_Data[31:24], H110};
  //   W112[31:0] = {Wr_En, Write_Data[31:24], H110}; Word_Align___1[22:0] = H110; b3[7:0] = Write_Data[31:24];
  //   W003[31:0] = {Wr_En, Write_Data[31:24], ALU[24:2]}; B000[31:0] = {Wr_En, Write_Data[7:0], ALU[24:2]};
  //   B011[31:0] = {Wr_En, Write_Data[7:0], ALU[24:2]}; B102[31:0] = {Wr_En, Write_Data[7:0], ALU[24:2]};
  //   B113[31:0] = {Wr_En, Write_Data[7:0], ALU[24:2]}; H000[31:0] = {Wr_En, Write_Data[7:0], ALU[24:2]};
  //   H011[31:0] = {Wr_En, Write_Data[7:0], ALU[24:2]}; H102[31:0] = {Wr_En, Write_Data[7:0], ALU[24:2]};
  //   H113[31:0] = {Wr_En, Write_Data[7:0], ALU[24:2]}; T000[31:0] = {Wr_En, Write_Data[7:0], ALU[24:2]};
  //   T011[31:0] = {Wr_En, Write_Data[7:0], ALU[24:2]}; T102[31:0] = {Wr_En, Write_Data[7:0], ALU[24:2]};
  //   T113[31:0] = {Wr_En, Write_Data[7:0], ALU[24:2]}; W000[31:0] = {Wr_En, Write_Data[7:0], ALU[24:2]};
  //   W011[31:0] = {Wr_En, Write_Data[7:0], ALU[24:2]}; W102[31:0] = {Wr_En, Write_Data[7:0], ALU[24:2]};
  //   W113[31:0] = {Wr_En, Write_Data[7:0], ALU[24:2]}; Word_Align[22:0] = ALU[24:2]; b0[7:0] = Write_Data[7:0];
  //   wen = Wr_En

  // Notes on the sheet:
  //    (00) Byte
  //   (01) Half
  //   (10) Tronple
  //   (11) Word
  //   0
  //   1
  //   2
  //   3
  //   0
  //   1
  //   2
  //   3
  //   0
  //   1
  //   2
  //   3
  //   0
  //   1
  //   2
  //   3
  //   00
  //   0
  //   1
  //   2
  //   3
  //   0
  //   1
  //   2
  //   3
  //   0
  //   1
  //   2
  //   3
  //   0
  //   1
  //   2
  //   3
  //   01
  //   Encoding = RAM# | Byte Index
  //   0
  //   1
  //   2
  //   3
  //   0
  //   1
  //   2
  //   3
  //   0
  //   1
  //   2
  //   3
  //   0
  //   1
  //   2
  //   3
  //   10
  //   0
  //   1
  //   2
  //   3
  //   0
  //   1
  //   2
  //   3
  //   0
  //   1
  //   2
  //   3
  //   0
  //   1
  //   2
  //   3
  //   11
  //   Byte 0
  //   Byte 1
  //   Byte 2
  //   Byte 3
endmodule

module Extend_Byte_S (
  input  [7:0] In,
  output [31:0] Out
);

  assign Out = {{24{In[7]}}, In};  // Bit_Extender bit_extender_1
endmodule

module Extend_Byte_U (
  input  [7:0] In,
  output [31:0] Out
);

  assign Out = {{24{1'b0}}, In};  // Bit_Extender bit_extender_1
endmodule

module Extend_Half_S (
  input  [15:0] In,
  output [31:0] Out
);

  assign Out = {{16{In[15]}}, In};  // Bit_Extender bit_extender_1
endmodule

module Extend_Half_U (
  input  [15:0] In,
  output [31:0] Out
);

  assign Out = {{16{1'b0}}, In};  // Bit_Extender bit_extender_1
endmodule

module Extend_Tronple_S (
  input  [23:0] In,
  output [31:0] Out
);

  assign Out = {{8{In[23]}}, In};  // Bit_Extender bit_extender_1
endmodule

module Extend_Tronple_U (
  input  [23:0] In,
  output [31:0] Out
);

  assign Out = {{8{1'b0}}, In};  // Bit_Extender bit_extender_1
endmodule

module Microcode (
  input  [31:0] Instr,
  output [22:0] Microcode
);

  ROM #(.addrWidth(12), .dataWidth(23)) rom_1 (
    .addr({Instr[6:0], Instr[14:12], Instr[30], Instr[25]}), .data(Microcode));  // open: sel

  // Notes on the sheet:
  //   22 = Invalid Instr
  //   21 = Stop Exec?
  //   20-18 = Imm Enc
  //   17 = Unsigned BComp?
  //   16-15 = BComp
  //   14 = Next PC Uncond
  //   13 = Branch?
  //   12 = ALU Input 1
  //   11 = ALU Input 2
  //   10-7 = ALU Op
  //   6-5 = RAM #
  //   4 = RAM Write Enable
  //   3 = RAM Read Unsigned?
  //   2-1 = WB Select
  //   0 = Register Write Enable
  //   Microcode
  //   contents of rom_1 (hex, n*v repeats v):
  //   96*600000 4*1005 4*1025 4*1065 4*600000 4*100d 4*102d 488*600000 4*1003 1303 600000 600000 600000
  //   4*1483 4*1503 4*1683 1383 600000 1403 600000 4*1583 4*1603 96*600000 32*101003 352*600000 4*41010
  //   4*41030 4*41070 500*600000 1803 1903 1883 600000 1b03 1983 600000 600000 1c83 600000 600000 600000
  //   1d03 600000 600000 600000 1e83 1a03 600000 600000 1b83 600000 1c03 600000 1d83 1a83 600000 600000
  //   1e03 99*600000 32*100703 1376*600000 4*92000 4*9a000 8*600000 4*82000 4*8a000 4*a2000 4*aa000
  //   96*600000 4*5001 252*600000 32*c4001 96*600000 200000 415*600000
endmodule
