// Logisim project interface.circ as structural Verilog: 1 circuit, main circuit main
module main (
);

  wire button_2_out, clk, clock_1_out, END, ERR, or_1_out, RESET;
  wire [31:0] INSTR, main_1_x0, main_1_x1, main_1_x2, main_1_x3, main_1_x4, main_1_x5, main_1_x6, main_1_x7,
       main_1_x8, main_1_x9, main_1_x10, main_1_x11, main_1_x12, main_1_x13, main_1_x14, main_1_x15,
       main_1_x16, main_1_x17, main_1_x18, main_1_x19, main_1_x20, main_1_x21, main_1_x22, main_1_x23,
       main_1_x24, main_1_x25, main_1_x26, main_1_x27, main_1_x28, main_1_x29, main_1_x30, main_1_x31, PC;

  cpu_main main_1 (
    .x0(main_1_x0), .x1(main_1_x1), .x2(main_1_x2), .x3(main_1_x3), .x4(main_1_x4), .x5(main_1_x5),
    .x6(main_1_x6), .x7(main_1_x7), .x8(main_1_x8), .x9(main_1_x9), .x10(main_1_x10), .x11(main_1_x11),
    .x12(main_1_x12), .x13(main_1_x13), .x14(main_1_x14), .x15(main_1_x15), .x16(main_1_x16),
    .x17(main_1_x17), .x18(main_1_x18), .x19(main_1_x19), .x20(main_1_x20), .x21(main_1_x21),
    .x22(main_1_x22), .x23(main_1_x23), .x24(main_1_x24), .x25(main_1_x25), .x26(main_1_x26),
    .x27(main_1_x27), .x28(main_1_x28), .x29(main_1_x29), .x30(main_1_x30), .x31(main_1_x31), .PC(PC),
    .Instruction(INSTR), .RESET(RESET), .End(END), .Error(ERR), .Clock(clk));
  // Probe on PC
  // Probe on main_1_x0
  // Probe on main_1_x1
  // Probe on main_1_x2
  // Probe on main_1_x3
  // Probe on main_1_x4
  // Probe on main_1_x5
  // Probe on main_1_x6
  // Probe on main_1_x7
  // Probe on main_1_x8
  // Probe on main_1_x9
  // Probe on main_1_x10
  // Probe on main_1_x11
  // Probe on main_1_x12
  // Probe on main_1_x13
  // Probe on main_1_x14
  // Probe on main_1_x15
  // Probe on main_1_x16
  // Probe on main_1_x17
  // Probe on main_1_x18
  // Probe on main_1_x19
  // Probe on main_1_x20
  // Probe on main_1_x21
  // Probe on main_1_x22
  // Probe on main_1_x23
  // Probe on main_1_x24
  // Probe on main_1_x25
  // Probe on main_1_x26
  // Probe on main_1_x27
  // Probe on main_1_x28
  // Probe on main_1_x29
  // Probe on main_1_x30
  // Probe on main_1_x31
  LED u_END (.in(END));
  LED u_ERR (.in(ERR));
  Button button_1 (.out(RESET));
  Clock clock_1 (.out(clock_1_out));
  Button button_2 (.out(button_2_out));
  or or_1 (or_1_out, clock_1_out, button_2_out);
  ROM #(.addrWidth(24), .dataWidth(32)) rom_1 (.addr(PC[25:2]), .data(INSTR));  // open: sel
  and and_1 (clk, ~END, or_1_out, ~ERR);  // AND_Gate

  // Notes on the sheet:
  //   Program
  //   contents of rom_1 (hex, n*v repeats v):
  //   fff00113 12345437 67840413 8402b3 840333 8403b3 2b3 333 3b3 22b00493 84a023 4a283 528333 5283b3 2b3
  //   333 3b3 4a283 54a223 44a303 2b3 333 100293 200293 8002b3 500333 5003b3 500e33 2b3 333 3b3 e33 42003
  //   33 29a00013 2b3 4a003 2023 42303 2b3 333
endmodule
